// Logisim project multiplexer.circ as structural Verilog
module multiplexer2way (
  input  w,
  input  S,
  input  x,
  output out
);

  wire and_1_out, and_2_out, not_1_out;

  not not_1 (not_1_out, S);
  and and_1 (and_1_out, w, not_1_out);
  and and_2 (and_2_out, S, x);
  or or_1 (out, and_1_out, and_2_out);
endmodule

module multiplexer4way (
  input  in_1,
  input  in_2,
  input  w,
  input  x,
  input  y,
  input  z,
  output out_7
);

  wire multiplexer2way_1_out, multiplexer2way_2_out;

  multiplexer2way multiplexer2way_1 (.w(w), .x(x), .S(in_2), .out(multiplexer2way_1_out));
  multiplexer2way multiplexer2way_2 (.w(y), .x(z), .S(in_2), .out(multiplexer2way_2_out));
  multiplexer2way multiplexer2way_3 (.w(multiplexer2way_1_out), .x(multiplexer2way_2_out), .S(in_1), .out(out_7));
endmodule
