// Logisim project project2_main.circ as structural Verilog: 1 circuit, main circuit main
module main (
  input  [3:0] in_1,
  input  [3:0] in_2
);

  wire adder4bit_1_c_2, adder4bit_1_f0, adder4bit_1_f1, adder4bit_1_f2, adder4bit_1_f3, doubledabble_1_f0,
       doubledabble_1_f1, doubledabble_1_f2, doubledabble_1_f3, doubledabble_1_g0, doubledabble_1_g1,
       doubledabble_1_g2, doubledabble_1_g3, hex_7seg_driver_1_p5, hex_7seg_driver_1_p6,
       hex_7seg_driver_1_p7, hex_7seg_driver_1_p8, hex_7seg_driver_1_p9, hex_7seg_driver_2_p5,
       hex_7seg_driver_2_p6, hex_7seg_driver_2_p7, hex_7seg_driver_2_p8, hex_7seg_driver_2_p9,
       hex_7seg_driver_2_p10, hex_7seg_driver_2_p11, hex_7seg_driver_2_p12, hex_7seg_driver_2_p13,
       hex_7seg_driver_3_p4, hex_7seg_driver_3_p5, hex_7seg_driver_3_p6, hex_7seg_driver_3_p7,
       hex_7seg_driver_4_p6, hex_7seg_driver_4_p7, hex_7seg_driver_4_p8, hex_7seg_driver_4_p9,
       hex_7seg_driver_4_p10, hex_7seg_driver_4_p11, hex_7seg_driver_4_p12, hex_7seg_driver_4_p13,
       hex_7seg_driver_4_p14, hex_7seg_driver_4_p15;

  adder4bit adder4bit_1 (
    .a3(in_1[3]), .a2(in_1[2]), .a1(in_1[1]), .a0(in_1[0]), .b3(in_2[3]), .b2(in_2[2]), .b1(in_2[1]),
    .b0(in_2[0]), .c(1'b0), .c_2(adder4bit_1_c_2), .f3(adder4bit_1_f3), .f2(adder4bit_1_f2),
    .f1(adder4bit_1_f1), .f0(adder4bit_1_f0));
  doubledabble doubledabble_1 (
    .a4(adder4bit_1_c_2), .a3(adder4bit_1_f3), .a2(adder4bit_1_f2), .a1(adder4bit_1_f1), .a0(adder4bit_1_f0),
    .f3(doubledabble_1_f3), .f2(doubledabble_1_f2), .f1(doubledabble_1_f1), .f0(doubledabble_1_f0),
    .g3(doubledabble_1_g3), .g2(doubledabble_1_g2), .g1(doubledabble_1_g1), .g0(doubledabble_1_g0));
  // hex_7seg_driver hex_7seg_driver_1: pin names not known; wires that end beside it: in_2[0], in_2[1], in_2[2], in_2[3], hex_7seg_driver_1_p5, hex_7seg_driver_1_p6, hex_7seg_driver_1_p7, hex_7seg_driver_1_p8, hex_7seg_driver_1_p9
  // hex_7seg_driver hex_7seg_driver_2: pin names not known; wires that end beside it: in_1[0], in_1[1], in_1[2], in_1[3], hex_7seg_driver_2_p5, hex_7seg_driver_2_p6, hex_7seg_driver_2_p7, hex_7seg_driver_2_p8, hex_7seg_driver_2_p9, hex_7seg_driver_2_p10, hex_7seg_driver_2_p11, hex_7seg_driver_2_p12, hex_7seg_driver_2_p13
  // hex_7seg_driver hex_7seg_driver_3: pin names not known; wires that end beside it: doubledabble_1_g0, doubledabble_1_g1, doubledabble_1_g2, hex_7seg_driver_3_p4, hex_7seg_driver_3_p5, hex_7seg_driver_3_p6, hex_7seg_driver_3_p7
  // hex_7seg_driver hex_7seg_driver_4: pin names not known; wires that end beside it: doubledabble_1_g3, doubledabble_1_f0, doubledabble_1_f1, doubledabble_1_f2, doubledabble_1_f3, hex_7seg_driver_4_p6, hex_7seg_driver_4_p7, hex_7seg_driver_4_p8, hex_7seg_driver_4_p9, hex_7seg_driver_4_p10, hex_7seg_driver_4_p11, hex_7seg_driver_4_p12, hex_7seg_driver_4_p13, hex_7seg_driver_4_p14, hex_7seg_driver_4_p15
  _7_Segment_Display u_7_segment_display_1 (
    .g(hex_7seg_driver_2_p13), .f(hex_7seg_driver_2_p12), .a(hex_7seg_driver_2_p7), .b(hex_7seg_driver_2_p8),
    .e(hex_7seg_driver_2_p11), .d(hex_7seg_driver_2_p10), .c(hex_7seg_driver_2_p9));  // open: dp
  _7_Segment_Display u_7_segment_display_2 (
    .g(hex_7seg_driver_2_p6), .f(hex_7seg_driver_2_p5), .a(hex_7seg_driver_1_p5), .b(hex_7seg_driver_1_p6),
    .e(hex_7seg_driver_1_p9), .d(hex_7seg_driver_1_p8), .c(hex_7seg_driver_1_p7));  // open: dp
  _7_Segment_Display u_7_segment_display_3 (
    .g(hex_7seg_driver_4_p15), .f(hex_7seg_driver_4_p14), .a(hex_7seg_driver_4_p9),
    .b(hex_7seg_driver_4_p10), .e(hex_7seg_driver_4_p13), .d(hex_7seg_driver_4_p12), .c(hex_7seg_driver_4_p11));  // open: dp
  _7_Segment_Display u_7_segment_display_4 (
    .g(hex_7seg_driver_4_p8), .f(hex_7seg_driver_4_p7), .a(hex_7seg_driver_3_p4), .b(hex_7seg_driver_3_p5),
    .e(hex_7seg_driver_4_p6), .d(hex_7seg_driver_3_p7), .c(hex_7seg_driver_3_p6));  // open: dp

  // Notes on the sheet:
  //   +
endmodule
